// Digital circuit circuito mealy.dig as structural Verilog
module circuito_mealy (
  input  X,
  input  CLK,
  output Detected
);

  wire and_1_out, and_2_out, and_3_out, and_4_out, E0_q, E1_q, not_1_out, not_2_out, or_1_out, or_2_out;

  not not_1 (not_1_out, E0_q);
  not not_2 (not_2_out, X);
  and and_1 (and_1_out, E0_q, X);
  and and_2 (and_2_out, E1_q, X);
  and and_3 (and_3_out, not_1_out, X);
  and and_4 (and_4_out, E1_q, X);
  or or_1 (or_1_out, and_1_out, and_2_out);
  or or_2 (or_2_out, and_3_out, and_4_out);
  D_FF E1 (.D(or_1_out), .C(CLK), .Q(E1_q));  // open: nQ
  D_FF E0 (.D(or_2_out), .C(CLK), .Q(E0_q));  // open: nQ
  and and_5 (Detected, E1_q, E0_q, not_2_out);
endmodule
